# Fritzing sketch pythonShutdownWiring (saved by Fritzing 0.9.9b)

parts:
  LED1 = LED - 5mm [color="Red (633nm)" package="5 mm [THT]"]
  S1 = Pushbutton [package="[THT]"]
  R1 = Resistor [tolerance=±5% resistance=330 package=THT]
  Mod1 = Raspberry Pi 4B

nets:
  N1: LED1.cathode, R1.Pin_0, Mod1.GPIO6
  N2: LED1.anode, Mod1.GPIO16
  N3: S1.Pin_1, S1.Pin_2, R1.Pin_1, Mod1.GND
  N4: S1.Pin_3, S1.Pin_4, Mod1.GPIO17

custom parts:
  Raspberry Pi 4B: The RPi4B, a faster version of the awesome Raspberry Pi 3 ARM Board with 40 pin gpio. Ready for special Raspberry Pi B+ and RPi2 Hat (Hardware attached (on) top) new features: The most surprising change for the Pi 4B is that it is available with three different amounts of fast DDR4 SDRAM memory; 1GB, 2GB, or 4GB. Combined with a newer 1.5GHz quad-core processor, the Pi 4B can run larger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
